# Fritzing sketch Sale_Bird_Ultrasonic_20151016 (saved by Fritzing 0.9.2b)
breadboards: 1

parts:
  元件1 = Arduino Nano (Rev3.0)
  Onderdeel2 = SRF05 Ultrasonic Rangefinder
  U1 = SWITCH_SPDT [package=kps-1290]
  VCC2 = 4 x AAA Battery Mount
  S1 = Toggle Switch [package=THT]
  R1 = Resistor [tolerance=±5% resistance=220 package=THT]
  R2 = Resistor [tolerance=±5% resistance=220 package=THT]
  LED1 = RGB LED (com. cathode, rgb) [package="5 mm [THT]"]
  R3 = Resistor [tolerance=±5% resistance=220 package=THT]
  R4 = Resistor [tolerance=±5% resistance=220 package=THT]
  R5 = Resistor [tolerance=±5% resistance=220 package=THT]
  Q1 = TRANSISTOR_NPN [package=to-92-ammo]
  Q2 = TRANSISTOR_NPN [package=to-92-ammo]
  U3 = 3.5mm Audio Jack [package=audio-jack-3.5mm-smd]

nets:
  N1: 元件1.D1/TX, Q1.B
  N2: 元件1.D0/RX, Q2.B
  GND: 元件1.GND, Onderdeel2.GND, VCC2.-, R1.Pin_0, R2.Pin_0, LED1.green_anode, Q1.C, Q2.E
  N3: 元件1.D3, Onderdeel2.Trig
  N4: 元件1.D4, Onderdeel2.Echo
  N5: 元件1.D7, R4.Pin_1
  N6: 元件1.D8, R3.Pin_1
  N7: 元件1.VIN, U1.P
  5V: 元件1.5V, Onderdeel2.VCC, S1.COM
  N8: 元件1.A1, S1.L2, R2.Pin_1
  N9: 元件1.A0, S1.L1, R1.Pin_1
  N10: 元件1.D13/SCK, R5.Pin_1
  N11: Q1.E, U3.RIGHT
  N12: Q2.C, U3.LEFT
